# Fritzing sketch BasementDoor (saved by Fritzing 0.9.3b)
circuit board: 5.06511cm x 4.77127cm
breadboards: 1

parts:
  WeMos_D1_Mini1 = WeMos D1 Mini
  Q1 = TRANSISTOR_NPN [package=to-92-ammo]
  RFID = female pin header, 4 pins [form="♀ (female)"]
  R1 = Resistor [tolerance=±5% resistance=220 package=THT]
  D1 = Rectifier Diode [part_number=1N4001 package="300 mil [THT]"]
  Strike = female pin header, 2 pins [form="♀ (female)"]
  LED = female pin header, 4 pins [form="♀ (female)"]
  R3 = Resistor [tolerance=±5% resistance=220 package=THT]
  Reset = female pin header, 2 pins [form="♀ (female)"]
  Power = male pin header, 3 pins [form="♂ (male)"]
  LED_2 = female pin header, 2 pins [form="♀ (female)"]
  R2 = Resistor [tolerance=±5% resistance=220 package=THT]
  Sensors = female pin header, 4 pins [form="♀ (female)"]
  DHT1 = DHT11 Humitidy and Temperature Sensor

nets:
  3V3: WeMos_D1_Mini1.3V3, LED.pin1, R3.Pin_1, DHT1.VDD
  N1: WeMos_D1_Mini1.5V, RFID.pin2, Power.pin1
  N2: WeMos_D1_Mini1.D0, R2.Pin_0
  N3: WeMos_D1_Mini1.D2, R1.Pin_0
  N4: WeMos_D1_Mini1.D3, Sensors.pin3
  N5: WeMos_D1_Mini1.D4, Sensors.pin2
  N6: WeMos_D1_Mini1.D5, R3.Pin_0, DHT1.DATA
  N7: WeMos_D1_Mini1.D6, LED.pin4
  N8: WeMos_D1_Mini1.D7, LED.pin3
  N9: WeMos_D1_Mini1.D8, LED.pin2
  N10: WeMos_D1_Mini1.G, Q1.E, RFID.pin1, Power.pin2, LED_2.pin2
  N11: WeMos_D1_Mini1.RST, Reset.pin2
  N12: WeMos_D1_Mini1.RX, RFID.pin3
  N13: WeMos_D1_Mini1.TX, RFID.pin4
  N14: Q1.B, R1.Pin_1
  N15: Q1.C, D1.anode, Strike.pin2
  N16: D1.cathode, Strike.pin1, Power.pin3
  N17: Reset.pin1, Sensors.pin1, Sensors.pin4, DHT1.GND
  N18: LED_2.pin1, R2.Pin_1

notes:
  12v
  5v
  T R + -
  B R G +
  -

custom parts:
  DHT11 Humitidy and Temperature Sensor: DHT11 Humidity and Temperature Sensor
