# Fritzing sketch circuit (saved by Fritzing 0.9.3b)
circuit board: 8.46667cm x 5.64444cm
breadboards: 1

parts:
  Q1 = Basic FET P-Channel [package="TO220 [THT]"]
  WeMos_D1_Mini1 = WeMos D1 Mini
  R1 = Resistor [tolerance=±5% resistance=220 package=THT]
  R2 = Resistor [tolerance=±5% resistance=220 package=THT]
  J1 = male pin header, 2 pins [form="♂ (male)"]

nets:
  N1: Q1.gate, R1.Pin_0, R2.Pin_1
  N2: Q1.drain, J1.pin1
  N3: Q1.source, WeMos_D1_Mini1.G, R2.Pin_0, J1.pin2
  N4: WeMos_D1_Mini1.D1, R1.Pin_1
