# Fritzing sketch watering2 (saved by Fritzing 0.9.3b)
circuit board: 6.79663cm x 6.49046cm
breadboards: 1

parts:
  WeMos_D1_Mini1 = WeMos D1 Mini
  MPX5010DP_-_2 = MPX4250AP pressure sensor [part_number=MPX]
  D1 = Rectifier Diode [part_number=1N4001 package="300 mil [THT]"]
  R1 = Resistor [tolerance=±5% resistance=220 package=THT]
  Valve_2 = female pin header, 2 pins [form="♀ (female)"]
  Moist_1 = female pin header, 3 pins [form="♀ (female)"]
  DHT1 = DHT11 Humitidy and Temperature Sensor
  Q2 = NPN-Transistor [package="TO92 [THT]"]
  D2 = Rectifier Diode [part_number=1N4001 package="300 mil [THT]"]
  Q3 = NPN-Transistor [package="TO92 [THT]"]
  MPX5010DP1_-_1 = MPX4250AP pressure sensor [part_number=MPX]
  D3 = Rectifier Diode [part_number=1N4001 package="300 mil [THT]"]
  Reset = male pin header, 2 pins [form="♂ (male)"]
  12V_to_5V = female pin header, 4 pins [form="♀ (female)"]
  R3 = Resistor [tolerance=±5% resistance=220 package=THT]
  R2 = Resistor [tolerance=±5% resistance=220 package=THT]
  D4 = Rectifier Diode [part_number=1N4001 package="300 mil [THT]"]
  Valve_1 = female pin header, 2 pins [form="♀ (female)"]
  R4 = Resistor [tolerance=±5% resistance=220 package=THT]
  Moist_2 = female pin header, 3 pins [form="♀ (female)"]
  Q5 = Basic FET N-Channel [package="TO220 [THT]"]
  Q6 = Basic FET N-Channel [package="TO220 [THT]"]
  12V = female pin header, 2 pins [form="♀ (female)"]
  R5 = Resistor [tolerance=±5% resistance=220 package=THT]
  R6 = Resistor [tolerance=±5% resistance=220 package=THT]

nets:
  3V3: WeMos_D1_Mini1.3V3, DHT1.VDD
  N1: WeMos_D1_Mini1.5V, MPX5010DP_-_2.Vs, D2.cathode, MPX5010DP1_-_1.Vs, D3.cathode, 12V_to_5V.pin1
  N2: WeMos_D1_Mini1.A0, MPX5010DP_-_2.V_out, MPX5010DP1_-_1.V_out
  N3: WeMos_D1_Mini1.D0, Moist_2.pin3
  N4: WeMos_D1_Mini1.D1, R3.Pin_1
  N5: WeMos_D1_Mini1.D2, R2.Pin_1
  N6: WeMos_D1_Mini1.D3, Moist_1.pin1
  N7: WeMos_D1_Mini1.D4, DHT1.DATA
  N8: WeMos_D1_Mini1.D5, Moist_2.pin1
  N9: WeMos_D1_Mini1.D6, Moist_1.pin3
  N10: WeMos_D1_Mini1.D7, R4.Pin_0, R5.Pin_1
  N11: WeMos_D1_Mini1.D8, R1.Pin_0, R6.Pin_1
  N12: WeMos_D1_Mini1.G, Moist_1.pin2, DHT1.GND, Q2.E, Q3.E, Reset.pin1, 12V_to_5V.pin2, 12V_to_5V.pin3, Moist_2.pin2, Q5.source, Q6.source, 12V.pin1, R5.Pin_0, R6.Pin_0
  N13: WeMos_D1_Mini1.RST, Reset.pin2
  N14: MPX5010DP_-_2.GND, Q2.C, D2.anode
  N15: D1.cathode, Valve_2.pin1, 12V_to_5V.pin4, D4.cathode, Valve_1.pin1, 12V.pin2
  N16: D1.anode, Valve_2.pin2, Q5.drain
  N17: R1.Pin_1, Q5.gate
  N18: Q2.B, R2.Pin_0
  N19: Q3.B, R3.Pin_0
  N20: Q3.C, MPX5010DP1_-_1.GND, D3.anode
  N21: D4.anode, Valve_1.pin2, Q6.drain
  N22: R4.Pin_1, Q6.gate

notes:
  +
  -

custom parts:
  DHT11 Humitidy and Temperature Sensor: DHT11 Humidity and Temperature Sensor
