# Fritzing sketch WallSwitch (saved by Fritzing 0.9.3b)
circuit board: 6.09504cm x 3.91837cm
perfboards: 1

parts:
  R1 = Resistor [tolerance=±5% resistance=220 package=THT]
  Screen = male pin header, 4 pins [form="♂ (male)"]
  IR_LED = male pin header, 2 pins [form="♂ (male)"]
  Motion = male pin header, 3 pins [form="♂ (male)"]
  Power = Screw terminal - 2 pins [package=THT]
  Light = Screw terminal - 2 pins [package=THT]
  IN- = female pin header, 1 pin [form="♀ (female)"]
  IN+ = female pin header, 1 pin [form="♀ (female)"]
  OUT+ = female pin header, 1 pin [form="♀ (female)"]
  OUT- = female pin header, 1 pin [form="♀ (female)"]
  WeMos_D1_Mini1 = WeMos D1 Mini
  Relay_2 = female pin header, 1 pin [form="♀ (female)"]
  Relay_3 = female pin header, 1 pin [form="♀ (female)"]
  Relay_4 = female pin header, 1 pin [form="♀ (female)"]
  Relay_1 = female pin header, 1 pin [form="♀ (female)"]
  L = male pin header, 1 pin [form="♂ (male)"]

nets:
  N1: R1.Pin_0, WeMos_D1_Mini1.D2
  N2: R1.Pin_1, IR_LED.pin1
  N3: Screen.pin1, IR_LED.pin2, Motion.pin2, OUT-.pin1, WeMos_D1_Mini1.G, Relay_1.pin1
  N4: Screen.pin2, WeMos_D1_Mini1.D4
  N5: Screen.pin3, WeMos_D1_Mini1.D7
  N6: Screen.pin4, Motion.pin1, OUT+.pin1, WeMos_D1_Mini1.5V
  N7: Motion.pin3, WeMos_D1_Mini1.D5
  N8: Power.pin1, Light.pin2, IN-.pin1
  N9: Power.pin2, IN+.pin1, Relay_3.pin1
  N10: Light.pin1, Relay_4.pin1
  N11: WeMos_D1_Mini1.D0, L.pin1
  N12: WeMos_D1_Mini1.D1, Relay_2.pin1

notes:
  +
